# Fritzing sketch esp8266_dht22 (saved by Fritzing 0.9.2b)
breadboards: 1

parts:
  U1 = ESP8266 WiFi Module [part_number=ESP8266]
  Reset = Momentary Switch [package=ksa_sealed_tac_switch]
  DHT1 = DHT22 Humidity and Temperature Sensor
  DHT_pullup = Resistor [tolerance=±5% resistance=10k package=THT]
  Reset_2 = Resistor [tolerance=±5% resistance=10k package=THT]
  GPI0 = Resistor [tolerance=±5% resistance=10k package=THT]
  power_filter = Electrolytic Capacitor [capacitance=22µF package="100 mil [THT, electrolytic]"]
  CH_PD = Resistor [tolerance=±5% resistance=10k package=THT]
  DTR = Resistor [tolerance=±5% resistance=470 package=THT]
  VReg = Voltage Regulator AMS1117 [package=sot223]
  J1 = Generic male header - 3 pins [form="♀ (female)" package=THT]
  J2 = Generic male header - 3 pins [form="♀ (female)" package=THT]
  Deep_Sleep = Resistor [tolerance=±5% resistance=470 package=THT]
  GPIO15 = Resistor [tolerance=±5% resistance=10k package=THT]

nets:
  N1: U1.RXD, J2.Pin_3
  N2: U1.GPIO_0, GPI0.Pin_0, DTR.Pin_0
  N3: U1.CH_PD, CH_PD.Pin_1
  GND: U1.GND, Reset.3, Reset.4, DHT1.GND, power_filter.-, VReg.GND, J1.Pin_3, GPIO15.Pin_1
  N4: U1.TXD, J2.Pin_2
  N5: U1.GPIO_15, GPIO15.Pin_0
  N6: U1.GPIO_16, Deep_Sleep.Pin_0
  N7: U1.GPIO_13, DHT1.DATA, DHT_pullup.Pin_0
  N8: U1.REST, Reset.1, Reset.2, Reset_2.Pin_1, Deep_Sleep.Pin_1
  N9: DHT1.VDD, DHT_pullup.Pin_1, Reset_2.Pin_0, GPI0.Pin_1, power_filter.+, CH_PD.Pin_0, VReg.OUT
  N10: DTR.Pin_1, J2.Pin_1
  N11: VReg.IN, J1.Pin_2

custom parts:
  Generic male header - 3 pins: Generic male header
